# Fritzing sketch arroseur_pcb (saved by Fritzing 0.9.2b)
circuit board: 3.13029cm x 4.24508cm
breadboards: 1

parts:
  C3-105 = Ceramic Capacitor [capacitance=1µF package="200 mil [THT, multilayer]"]
  C2-105 = Ceramic Capacitor [capacitance=1µF package="200 mil [THT, multilayer]"]
  D2 = Rectifier Diode [part_number=1N4001 package="300 mil [THT]"]
  R3 = Resistor [tolerance=±5% resistance=2.2k package=THT]
  TIP121 = Voltage Regulator - 5V [package="TO220 [THT]"]
  U1 = attiny85 [package=dip]
  J17 = female pin header, 3 pins [form="♀ (female)"]
  J18 = female pin header, 1 pin [form="♀ (female)"]
  J19 = female pin header, 1 pin [form="♀ (female)"]
  J20 = female pin header, 1 pin [form="♀ (female)"]
  J21 = screw terminal, 2 pins
  J22 = screw terminal, 2 pins
  TIP122 = Voltage Regulator - 5V [package="TO220 [THT]"]
  J16 = female pin header, 4 pins [form="♀ (female)"]
  J23 = female pin header, 1 pin [form="♀ (female)"]

nets:
  N1: C3-105.0, C2-105.0, U1.Pin_4, J18.pin1, J21.pin2, TIP122.GND, J16.pin2
  N2: C3-105.1, D2.cathode, J21.pin1, J22.pin2, TIP122.input_voltage
  N3: C2-105.1, U1.Pin_8, J19.pin1, TIP122.output_voltage
  N4: D2.anode, TIP121.GND, J22.pin1
  N5: R3.Pin_0, TIP121.input_voltage
  N6: R3.Pin_1, U1.Pin_7, J17.pin1
  N7: TIP121.output_voltage, J16.pin3
  N8: U1.Pin_1, J20.pin1
  N9: U1.Pin_2, J16.pin1
  N10: U1.Pin_3, J23.pin1
  N11: U1.Pin_5, J17.pin3
  N12: U1.Pin_6, J17.pin2, J16.pin4

notes:
  -
  P
  +
